# Fritzing sketch teplitsa_scheme (saved by Fritzing 0.9.5d)
breadboards: 1

parts:
  U1 = ESP32S-HiLetgo [part_number=ESP32S-HiLetgo]
  U3 = RELAY [package=relay-jzc]
  JACK1 = 2.1mm Barrel Jack with Terminal Block
  Компонент1 = Soil Moisture Sensor
  WATER_PUMP1 = water pump/motor
  A1 = Dryer heater
  DS1 = DS18B20 1-Wire Temperature Sensor Probe
  Q2 = Basic FET N-Channel [package="TO220 [THT]"]
  M3 = RioRand LM2596
  R1 = Resistor [tolerance=±5% resistance=10000 package="0402 [SMD]"]

nets (from the breadboard view):
  N1: U1.GPIO32, U3.MAIN
  N2: U1.GPIO33, DS1.DQ
  N3: U1.GPIO25, Компонент1.SIG
  N4: U1.GPIO26, Q2.gate, R1.Pin_1
  GND: U1.GND, U3.COIL1, JACK1.NEG, Компонент1.GND, WATER_PUMP1.pin_1, DS1.GND, Q2.source, M3.Pin_2, M3.Pin_4, R1.Pin_0
  N5: U1.VIN, M3.Pin_3
  N6: U3.COIL2, JACK1.POS, A1.Pin_1, M3.Pin_1
  N7: U3.NC, WATER_PUMP1.pin_2
  VCC: Компонент1.VCC, DS1.VDD
  N8: A1.Pin_2, Q2.drain

custom parts:
  ESP32S-HiLetgo: HiLetgo ESP-WROOM-32 ESP32 ESP-32S Development Board 2.4GHz Dual-Mode WiFi + Bluetooth Dual Cores Microcontroller The ESP32 integrated with Antenna switches, RF Balun, power amplifiers, low-noise amplifiers, filters, and management modules, and the entire solution occupies the least area of PCB. 2.4 GHz Wi-Fi plus Bluetooth dual-mode chip, with TSMC Ultra-low power consumption 40nm technology,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
  water pump/motor: WATER PUMP BY ARDUBLOCKTR
  Dryer heater: Dryer heater.
